# Fritzing sketch fritzingDiagram (saved by Fritzing 0.9.3b)
breadboards: 2

parts:
  Part1 = Arduino Uno (Rev3)
  Part2 = Bluetooth HC-05 Macho
  hc-sr1 = hc-sr04
  hc-sr2 = hc-sr04
  LED1 = LED - 5mm [color="White (6500K)" package="5 mm [THT]"]
  LED2 = LED - 5mm [color="White (6500K)" package="5 mm [THT]"]
  LED3 = LED - 5mm [color="White (6500K)" package="5 mm [THT]"]
  LED4 = LED - 5mm [color="White (6500K)" package="5 mm [THT]"]
  LED5 = LED - 5mm [color="White (6500K)" package="5 mm [THT]"]
  LED6 = LED - 5mm [color="White (6500K)" package="5 mm [THT]"]
  IC2 = uM-FPUv3 [package=THT]
  R1 = Resistor [tolerance=±5% resistance=220 package=THT]
  R2 = Resistor [tolerance=±5% resistance=220 package=THT]
  R3 = Resistor [tolerance=±5% resistance=220 package=THT]
  R4 = Resistor [tolerance=±5% resistance=220 package=THT]
  R5 = Resistor [tolerance=±5% resistance=220 package=THT]
  R6 = Resistor [tolerance=±5% resistance=220 package=THT]
  R7 = Resistor [tolerance=±5% resistance=220 package=THT]

nets:
  N1: Part1.A4/SDA, IC2.AN0
  N2: Part1.A5/SCL, IC2.MCLR
  N3: Part1.D0/RX, Part2.RXD
  N4: Part1.D1/TX, Part2.TXD
  N5: Part1.D3_PWM, hc-sr2.Echo
  N6: Part1.D4, hc-sr2.Trig
  N7: Part1.D5_PWM, hc-sr1.Echo
  N8: Part1.D6_PWM, hc-sr1.Trig
  VCC: Part1.5V, Part2.VCC, hc-sr1.VCC, hc-sr2.VCC, IC2.AVDD_-_Analogue_Supply, R6.Pin_0
  GND: Part1.GND, Part2.GND, hc-sr1.GND, hc-sr2.GND, IC2.AN1, IC2.CS, IC2.EXTIN, R1.Pin_0, R2.Pin_0, R3.Pin_0, R4.Pin_1, R5.Pin_1, R7.Pin_1
  N9: LED1.cathode, R5.Pin_0
  N10: LED1.anode, IC2.AVSS_-_Analogue_Ground
  N11: LED2.cathode, R7.Pin_0
  N12: LED2.anode, IC2.I2C_Data_/_SPI_Data_In
  N13: LED3.cathode, R3.Pin_1
  N14: LED3.anode, IC2.0V
  N15: LED4.cathode, R2.Pin_1
  N16: LED4.anode, IC2.+V
  N17: LED5.cathode, R1.Pin_1
  N18: LED5.anode, IC2.OUT0
  N19: LED6.cathode, R4.Pin_0
  N20: LED6.anode, IC2.SPI_clock
  N21: IC2.OSC1, R6.Pin_1
